# Fritzing sketch Vreg (saved by Fritzing 0.9.3b)
stripboards: 1

parts:
  LM1085IT-3_3 = Voltage Regulator - Variable [package="TO220 [THT]"]  # not connected
  C1 = Tantalum Capacitor [capacitance=10µF voltage=20V package="100 mil [THT, tantalum]"]
  C2 = Tantalum Capacitor [capacitance=10µF voltage=20V package="100 mil [THT, tantalum]"]
  D1 = Rectifier Diode [part_number=1N4002 package="300 mil [THT]"]

nets:
  N1: C1.-, C2.+, D1.cathode
  N2: C1.+, C2.-, D1.anode

notes:
  GND
  9V In
  3.3V Out
