# Fritzing sketch ledmodule (saved by Fritzing 0.9.3b)

parts:
  LED1 = LED - 5mm [color="Green (565nm)" package="5 mm [THT]"]
  LED2 = LED - 5mm [color="Green (565nm)" current=20mA package="5 mm [THT]"]
  LED3 = LED - 5mm [color="Green (565nm)" package="5 mm [THT]"]
  LED4 = LED - 5mm [color="Green (565nm)" package="5 mm [THT]"]
  LED5 = LED - 5mm [color="Green (565nm)" package="5 mm [THT]"]
  LED6 = LED - 5mm [color="Green (565nm)" package="5 mm [THT]"]
  LED7 = LED - 5mm [color="Green (565nm)" package="5 mm [THT]"]
  LED8 = LED - 5mm [color="Green (565nm)" package="5 mm [THT]"]
  R2 = Resistor [tolerance=±2% resistance=10 package=THT]
  R1 = Resistor [tolerance=±2% resistance=10 package=THT]
  LED10 = LED - 5mm [color="Green (560nm)" package="5 mm [THT]"]
  LED11 = LED - 5mm [color="Green (565nm)" package="5 mm [THT]"]
  LED14 = LED - 5mm [color="Green (565nm)" package="5 mm [THT]"]
  LED15 = LED - 5mm [color="Green (565nm)" package="5 mm [THT]"]
  J1 = female pin header, 1 pin [form="♀ (female)"]
  J2 = male pin header, 1 pin [form="♂ (male)"]
  J3 = female pin header, 1 pin [form="♀ (female)"]
  J4 = male pin header, 1 pin [form="♂ (male)"]
  R3 = Resistor [tolerance=±5% resistance=180 package=THT]
  R4 = Resistor [tolerance=±5% resistance=330 package=THT]
  R5 = Resistor [tolerance=±5% resistance=12 package=THT]

nets:
  N1: LED1.cathode, LED8.anode
  14V: LED1.anode, LED2.anode, LED14.anode
  N2: LED2.cathode, LED3.anode
  N3: LED3.cathode, LED7.anode
  N4: LED4.cathode, LED5.anode
  N5: LED4.anode, LED8.cathode
  N6: LED5.cathode, R1.Pin_1
  N7: LED6.cathode, R2.Pin_1
  N8: LED6.anode, LED7.cathode
  N9: R2.Pin_0, R1.Pin_0, J1.pin1
  N10: LED10.cathode, J3.pin1
  N11: LED10.anode, LED11.cathode
  N12: LED11.anode, LED15.cathode
  N13: LED14.cathode, LED15.anode
  GND: J2.pin1, R3.Pin_0, R3.Pin_1, R4.Pin_0, R5.Pin_0
  N14: J4.pin1, R4.Pin_1, R5.Pin_1

notes:
  LED 42 DSK ON + LED 55 KEY ON
  LED 46 + LED 47
  Vr = 2,2V
  If = 20 mA
  Remove R3
  Replace with 12 Ohm
